# Fritzing sketch receiver (saved by Fritzing 0.9.3b)
breadboards: 1

parts:
  Part2 = Arduino Pro Mini (3.3V)  # not connected
  Part3 = RFM69 Breakout (915MHz) [part_number=WRL-12775]  # not connected
  J1 = Dagu DGServo 9g header connector (female) [package=THT]
  J2 = Dagu DGServo 9g header connector (female) [package=THT]
  LED1 = DUO LED RG [package="5 mm [THT]"]
  R1 = Resistor [tolerance=±5% resistance=330 package="0402 [SMD]"]
  U1 = attiny85 [package=dip]

nets:
  GND: J1.gnd, J2.gnd, U1.Pin_8
  VCC: J1.Vcc, J2.Vcc, U1.Pin_7
  N1: J1.pulse, J2.pulse, R1.Pin_1, U1.Pin_4
  N2: LED1.common_cathode, R1.Pin_0

notes:
  To Nintendo 64 Console

custom parts:
  RFM69 Breakout (915MHz): The RFM69HCW is an inexpensive and versatile radio module. You can use it to send text or binary data between two or hundreds of modules. It’s perfect for building inexpensive short-range wireless networks for home automation, citizen science, and more.
